# Fritzing sketch Wiring diagram (saved by Fritzing 0.9.4)
breadboards: 1

parts:
  U1 = ESP32-38PinWide [part_number=ESP32-38PinWide]
  J1 = Screw terminal - 2 pins [package=THT]
  J3 = screw terminal, 8 pins
  D1 = Rectifier Diode [part_number=1N4001 package="300 mil [THT]"]
  J2 = screw terminal, 11 pins

nets:
  N1: U1.3.3, J2.pin10
  N2: U1.GPIO32, J3.pin1
  N3: U1.GPIO33, J2.pin4
  N4: U1.GPIO25, J2.pin3
  N5: U1.GPIO26, J2.pin2
  N6: U1.GPIO27, J2.pin1
  N7: U1.GPIO12, J2.pin6
  N8: U1.GND, J1.pin1, J2.pin11
  N9: U1.GPIO13, J2.pin5
  N10: U1.VIN, D1.cathode, J2.pin9
  N11: U1.GPIO15, J3.pin3
  N12: U1.GPIO2, J2.pin8
  N13: U1.GPIO4, J2.pin7
  N14: U1.GPIO18, J3.pin8
  N15: U1.GPIO19, J3.pin7
  N16: U1.GPIO21, J3.pin6
  N17: U1.GPIO3, J3.pin5
  N18: U1.GPIO1, J3.pin4
  N19: U1.GPIO23, J3.pin2
  N20: J1.pin2, D1.anode

notes:
  Output
  Inputs
  Input
  GND         5V
  to 8ch Relay Board

custom parts:
  ESP32-38PinWide: Generic 38-Pin ESP32 with wide format (only access to one side of pins on a breadboard) based on Stephen Lilley's HiLetgo ESP-WROOM-32 ESP32 ESP-32S Development Board.
